# Fritzing sketch schematic (saved by Fritzing 1.0.5)
breadboards: 1

parts:
  CMJCU-812 = CJMCU-811
  CCS812 = Adafruit CCS811 [part_number="Adafruit #3566"]
  MQ3 = MQ-3 breakout
  MQ136 = Gas Sensor Breakout Board
  ESP33 = Heltec WiFi LoRa 32 V2 [part_number=HTIT-WB32LA]

nets:
  VCC: CMJCU-812.VCC, CCS812.3.3V, MQ3.VCC, MQ136.B1, MQ136.B2, ESP33.pin_16, ESP33.pin_17
  GND: CMJCU-812.GND, CCS812.GND, MQ3.GND, MQ136.GND, MQ136.H1, ESP33.GND
  N1: CMJCU-812.SCL, CMJCU-812.SDA, CCS812.SDA, CCS812.SCL, ESP33.pin_21, ESP33.pin_22
  N2: MQ136.A1, ESP33.pin_11

custom parts:
  CJMCU-811: The CCS811 is an ultra-low power digital gas sensor solution which integrates a metal oxide (MOX) gas sensor to detect a wide range of Volatile Organic Compounds (VOCs) for indoor air quality monitoring with a microcontroller unit (MCU), which includes an Analog-to-Digital converter (ADC), and an I²C interface.
  Adafruit CCS811: Breathe easy - we finally have an I2C VOC/eCO2 sensor in the Adafruit shop! Add air quality monitoring to your project and with an Adafruit CCS811 Air Quality Sensor Breakout. This sensor from AMS is a gas sensor that can detect a wide range of Volatile Organic Compounds (VOCs) and is intended for indoor air quality monitoring. When connected to your microcontroller (running our library code)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
  MQ-3 breakout: Alcohol sensor is capable of detecting alcohol (ethanol) particles on itself and gives the information in digital form back to us to manipulate with it. SKU:101251 • Voltage: 5V DC • Power: max 750mW • Measurement range: 0.04-4mg/L
